// Logisim project O0.circ as structural Verilog: 1 circuit, main circuit main
module main (
  input  I0,
  input  I1,
  input  I2,
  input  I3,
  output _00
);

  wire and_1_out, and_2_out, and_3_out, and_4_out, and_5_out, not_1_out, not_2_out, not_3_out, not_4_out,
       not_5_out, not_6_out, not_7_out, not_8_out, not_9_out, or_1_out, or_2_out;

  not not_1 (not_1_out, I0);
  not not_2 (not_2_out, I1);
  not not_3 (not_3_out, I1);
  not not_4 (not_4_out, I2);
  not not_5 (not_5_out, I3);
  not not_6 (not_6_out, I0);
  not not_7 (not_7_out, I2);
  not not_8 (not_8_out, I1);
  not not_9 (not_9_out, I3);
  and and_1 (and_1_out, not_1_out, not_2_out);
  and and_2 (and_2_out, not_3_out, not_4_out, not_5_out);
  and and_3 (and_3_out, not_6_out, not_7_out, I3);
  and and_4 (and_4_out, not_8_out, I2, I3);
  and and_5 (and_5_out, I0, I1, not_9_out);
  or or_1 (or_1_out, and_1_out, and_2_out);
  or or_2 (or_2_out, and_3_out, and_4_out);
  or or_3 (_00, or_1_out, or_2_out, and_5_out);

  // Notes on the sheet:
  //   I1'
  //   I2'
  //   I3'
  //   I0'
  //   I2'
  //   I3
  //   I1'
  //   I2
  //   I3
  //   I0
  //   I1
  //   I3'
  //   I0'
  //   I1'
  //   I0.I1.I3'
  //                                 (I0'.I1')+(I1'.I2'.I3')
  //    (I0'.I1'.I2)+(I1'.I2.I3)
endmodule
