// Logisim project O1.circ as structural Verilog: 1 circuit, main circuit main
module main (
  input  I0,
  input  I1,
  input  I2,
  input  I3,
  output O1
);

  wire and_1_out, and_2_out, and_3_out, not_1_out, not_2_out, not_3_out, not_4_out;

  not not_1 (not_1_out, I0);
  not not_2 (not_2_out, I1);
  not not_3 (not_3_out, I2);
  not not_4 (not_4_out, I3);
  and and_1 (and_1_out, not_1_out, I3);
  and and_2 (and_2_out, I2, I3);
  and and_3 (and_3_out, I0, I1, not_3_out);
  or or_1 (O1, and_1_out, and_2_out, and_3_out);
endmodule
