// Logisim project O3.circ as structural Verilog: 1 circuit, main circuit main
module main (
  input  I0,
  input  I1,
  input  I2,
  input  I3,
  output O3
);

  wire and_1_out, and_2_out, and_3_out, and_4_out, and_5_out, not_1_out, not_2_out, not_3_out, not_4_out;

  not not_1 (not_1_out, I0);
  not not_2 (not_2_out, I1);
  not not_3 (not_3_out, I2);
  not not_4 (not_4_out, I3);
  and and_1 (and_1_out, not_1_out, not_2_out, not_3_out);
  and and_2 (and_2_out, not_1_out, not_2_out, I3);
  and and_3 (and_3_out, I1, not_3_out, I3);
  and and_4 (and_4_out, I1, I2, not_4_out);
  and and_5 (and_5_out, I0, not_2_out, I2);
  or or_1 (O3, and_1_out, and_2_out, and_3_out, and_4_out, and_5_out);
endmodule
